# Fritzing sketch Mini_stepper_motor (saved by Fritzing 0.7.10b)
breadboards: 1

parts:
  M1 = Stepper Motor - Bipolar
  IC1 = L293D [package=THT]
  Arduino1 = Arduino
  Componente1 = Bluetooth Mate Silver

nets:
  N1: M1.A, IC1.Out_1_(_Controlled_by_Enable_1_)
  N2: M1.C, IC1.Out_2_(_Controlled_by_Enable_1_)
  N3: M1.B, IC1.Out_4_(_Controlled_by_Enable_2_)
  N4: M1.D, IC1.Out_3_(_Controlled_by_Enable_2_)
  5V: IC1.Enable_1, IC1.+Vmotor, IC1.Enable_2, IC1.+V, Arduino1.+5V
  N5: IC1.In_1, Arduino1.D8
  GND: IC1.0V
  N6: IC1.In_2, Arduino1.D9
  N7: IC1.In_3, Arduino1.D10
  N8: IC1.In_4, Arduino1.D11
  N9: Arduino1.D1TX, Componente1.RX_5V
  N10: Arduino1.D0RX, Componente1.TX_5V
